# Fritzing sketch UnitRoverSchem (saved by Fritzing 0.9.10b)
breadboards: 1

parts:
  Mod1 = Heltec WiFi LoRa 32 V2 [part_number=HTIT-WB32LA]
  M1 = gear-motor
  C1 = Capacitor Polarized [package=nippon_f80]
  B7_4V = LIPO-2000mAh [package=lipo-2000]
  10A_Fuse = FUSE [package=fuse_5mm]
  D1 = Rectifier Diode [part_number=1N4007 package="Melf DO-213 AB [SMD]"]
  D2 = Rectifier Diode [part_number=1N4007 package="Melf DO-213 AB [SMD]"]
  D3 = Rectifier Diode [part_number=1N4007 package="Melf DO-213 AB [SMD]"]
  D4 = Rectifier Diode [part_number=1N4007 package="Melf DO-213 AB [SMD]"]
  U2 = Voltage Regulator - 3.3V [package="TO220 [THT]"]
  R1 = TRIMPOT [maximum_resistance=10kΩ knob_status=50% power=0.5W package=trimpot-3mm-2]
  Q1 = NPN-Transistor [part_number=2N2222 package="TO92 [THT]"]
  Q2 = NPN-Transistor [part_number=2N2222 package="TO92 [THT]"]
  Q3 = NPN-Transistor [part_number=2N2222 package="TO92 [THT]"]
  Q4 = NPN-Transistor [part_number=2N2222 package="TO92 [THT]"]
  J1 = Infrared Proximity Sensor [distance_to_obstacle=50%]
  R3 = Resistor [package="2010 [SMD]"]
  R4 = Resistor [package="2010 [SMD]"]
  R5 = Resistor [package="2010 [SMD]"]
  R6 = Resistor [package="2010 [SMD]"]
  Enc1 = shaft encoder
  Part1 = IMU Digital Combo Board 6DOF

nets:
  VCC: Mod1.pin_16, Mod1.pin_17, U2.output_voltage, J1.Vcc, Enc1.VCC, Part1.3.3V
  GND: Mod1.GND, C1.-, B7_4V.-, D2.anode, D4.anode, U2.GND, R1.CW, Q2.E, Q4.E, J1.GND, Enc1.GND, Part1.GND
  N1: Mod1.pin_21, Mod1.pin_22, R1.WIPER
  N2: M1.pin_1, D3.anode, D4.cathode, Q3.E, Q4.C
  N3: M1.pin_2, D1.anode, D2.cathode, Q1.E, Q2.C
  N4: C1.+, 10A_Fuse.2, U2.input_voltage, R1.CCW
  N5: B7_4V.+, 10A_Fuse.1
  N6: D1.cathode, D3.cathode, Q1.C, Q3.C
  N7: Q1.B, R3.Pin_1
  N8: Q2.B, R4.Pin_1
  N9: Q3.B, R5.Pin_0
  N10: Q4.B, R6.Pin_0
  N11: R3.Pin_0, R6.Pin_1
  N12: R4.Pin_0, R5.Pin_1

notes:
  External battery voltage monitoring, shut off @ 3.2 V per cell!
  In2
  In1
  In1 = 0-1 (PWM),
  In2 = 0-1 (PWM),
  Set In2 to Low and In2
  H-Bridge and Motor x2
  ESP32 MCU
  IR_O
  2D LiDAR
  Optical Rotary Encoder
  x2
  6DOF IMU
  7.4 V 2S LiPO, 1000mAh

custom parts:
  Rectifier Diode: A smd rectifier diode
  NPN-Transistor: A standard NPN-transistor
  Resistor: Resistor Basic schematic elements and footprints for 0603, 1206, and PTH resistors.
